# Fritzing sketch Untitled Sketch 2 (saved by Fritzing 0.9.3b)
breadboards: 1

parts:
  Part1 = Arduino Uno (Rev3)
  Q1 = NPN-Transistor [package="TO92 [THT]"]
  Q2 = NPN-Transistor [package="TO92 [THT]"]
  Q3 = NPN-Transistor [package="TO92 [THT]"]
  J1 = shrouded pin header, 10 pins [form="♂ (shrouded male)"]  # not connected
  X1 = DB9 Connector [package=db9]  # not connected
  X2 = DB9 Connector [package=db9]  # not connected

nets:
  N1: Part1.D9_PWM, Q1.B
  N2: Part1.D5_PWM, Q3.B
  N3: Part1.D6_PWM, Q2.B
  N4: Q1.E, Q2.E, Q3.E
